# Fritzing sketch robotling_version1_1 (saved by Fritzing 0.9.3b)
circuit board: 6.62cm x 5.85cm
breadboards: 2

parts:
  Feather = Adafruit HUZZAH32 ESP32 Feather [part_number="Adafruit #3405"]
  Motors = female pin header, 4 pins [form="♀ (female)" part_number="Motor connector"]
  DRV8835 = DRV8835 [package="DIP (Dual Inline) [THT]"]
  MCP3208 = IC, DIP package, 16 pins [chip_label=MCP3208]
  C1 = Tantalum Capacitor [capacitance=1μF package="100 mil [THT, tantalum]"]
  Analog_In = female pin header, 8 pins [form="♀ (female)"]
  Analog_In_b = female pin header, 8 pins [form="♀ (female)"]
  Analog_In_c = female pin header, 8 pins [form="♀ (female)"]
  R1 = Resistor [tolerance=±5% resistance=8.2k package=THT]
  I2C = female pin header, 6 pins [form="♀ (female)"]
  J2 = male pin header, 2 pins [form="♂ (male)"]
  J2_b = male pin header, 2 pins [form="♂ (male)"]
  SN72AHCT125N = IC, DIP package, 14 pins [chip_label=SN72AHCT]
  C2 = Tantalum Capacitor [capacitance=1μF package="100 mil [THT, tantalum]"]
  DIO = female pin header, 4 pins [form="♀ (female)"]
  DIO_c = female pin header, 4 pins [form="♀ (female)"]
  DIO_b = female pin header, 4 pins [form="♀ (female)"]
  J1 = female pin header, 2 pins [form="♀ (female)"]
  LSM303 = Flora LSM303 Compass+Accel
  R2 = Resistor [tolerance=±5% resistance=8.2k package=THT]
  Bauteil1 = Lithium Ion Polymer Battery 3.7v 350mAh [part_number=2750]
  S1 = SPST Switch [package=switch-spdt]
  LED = female pin header, 3 pins [form="♀ (female)"]
  R3 = Resistor [tolerance=±5% resistance=680 package=THT]
  J3 = rounded female pin header, 4 pins [form="♀ (female rounded)"]
  J4 = female pin header, 2 pins [form="♀ (female)"]
  R4 = Resistor [tolerance=±5% resistance=680 package=THT]
  LED1 = LED - 3mm [color="Green (565nm)" package="3 mm [THT]"]
  R5 = Resistor [tolerance=±5% resistance=1k package=THT]

nets:
  N1: Feather.IO21, DRV8835.B/EN/IN2
  N2: Feather.IO16, J4.pin2, R5.Pin_1
  N3: Feather.MISO, MCP3208.pin12
  N4: Feather.MOSI, MCP3208.pin11
  N5: Feather.SCK, MCP3208.pin13
  N6: Feather.A5_IO4, MCP3208.pin10
  N7: Feather.A1_DAC1, DRV8835.B/PH/IN1
  N8: Feather.A0_DAC2, DRV8835.A/EN/IN2
  GND: Feather.GND, DRV8835.GNDd, DRV8835.GNDm, MCP3208.pin9, MCP3208.pin14, C1.-, Analog_In_b.pin1, Analog_In_b.pin2, Analog_In_b.pin3, Analog_In_b.pin4, Analog_In_b.pin5, Analog_In_b.pin6, Analog_In_b.pin7, Analog_In_b.pin8, I2C.pin6, SN72AHCT125N.pin1, SN72AHCT125N.pin4, SN72AHCT125N.pin7, SN72AHCT125N.pin10, SN72AHCT125N.pin13, C2.-, DIO_c.pin1, DIO_c.pin2, DIO_c.pin3, DIO_c.pin4, LSM303.GND, Bauteil1.negative, LED.pin2, J3.pin2, LED1.cathode, R5.Pin_0
  3.3V: Feather.3.3V, DRV8835.VCC, R1.Pin_0, I2C.pin5, J1.pin1, LSM303.3.3V, R2.Pin_0
  N9: Feather.VBAT, S1.P, J3.pin3
  N10: Feather.IO13_A12, SN72AHCT125N.pin12
  N11: Feather.IO27_A10, SN72AHCT125N.pin9
  N12: Feather.IO33_A9, SN72AHCT125N.pin5
  N13: Feather.IO15_A8, R3.Pin_1
  N14: Feather.IO32_A7, J2.pin1, J2.pin2
  N15: Feather.IO14_A6, DRV8835.A/PH/IN1
  N16: Feather.SCL, R1.Pin_1, I2C.pin4, LSM303.SCL
  N17: Feather.SDA, I2C.pin3, LSM303.SDA, R2.Pin_1
  N18: Motors.pin1, DRV8835.BOUT2
  N19: Motors.pin2, DRV8835.BOUT1
  N20: Motors.pin3, DRV8835.AOUT2
  N21: Motors.pin4, DRV8835.AOUT1
  N22: DRV8835.MODE, J1.pin2
  N23: DRV8835.VMM, MCP3208.pin15, MCP3208.pin16, C1.+, Analog_In_c.pin1, Analog_In_c.pin2, Analog_In_c.pin3, Analog_In_c.pin4, Analog_In_c.pin5, Analog_In_c.pin6, Analog_In_c.pin7, Analog_In_c.pin8, I2C.pin1, SN72AHCT125N.pin14, C2.+, DIO_b.pin1, DIO_b.pin2, DIO_b.pin3, DIO_b.pin4, LED.pin1, R4.Pin_0
  N24: DRV8835.VIN, J3.pin1
  N25: MCP3208.pin1, Analog_In.pin1
  N26: MCP3208.pin2, Analog_In.pin2
  N27: MCP3208.pin3, Analog_In.pin3
  N28: MCP3208.pin4, Analog_In.pin4
  N29: MCP3208.pin5, Analog_In.pin5
  N30: MCP3208.pin6, Analog_In.pin6
  N31: MCP3208.pin7, Analog_In.pin7
  N32: MCP3208.pin8, Analog_In.pin8
  N33: I2C.pin2, J2_b.pin1
  N34: J2_b.pin2, SN72AHCT125N.pin2
  N35: SN72AHCT125N.pin3, DIO.pin1
  N36: SN72AHCT125N.pin6, DIO.pin2
  N37: SN72AHCT125N.pin8, DIO.pin4
  N38: SN72AHCT125N.pin11, DIO.pin3
  N39: Bauteil1.positive, S1.S
  N40: LED.pin3, R3.Pin_0
  N41: J3.pin4, J4.pin1
  N42: R4.Pin_1, LED1.anode

notes:
  2
  1
  -MA-
  -MB-
  Vo
  Vi
  gnd
  7
  Ai G 5V
  3V
  sda
  scl
  5V
  G 5V D
  3
  0
  D3
  >I2C
  >DIO
  (+)
  (-)
  OFF
  5V G Dta
  Robotling
  shdn
  v1.1

custom parts:
  DRV8835: Motor driver by Pololu
  Flora LSM303 Compass+Accel: Add motion and direction sensing to your wearable FLORA project with this high precision 3-axis Accelerometer+Compass sensor. Inside are two sensors, one is a classic 3-axis accelerometer, which can tell you which direction is down towards the Earth (by measuring gravity) or how fast the board is accelerating in 3D space. The other is a magnetometer that can sense where the strongest magnetic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
  Lithium Ion Polymer Battery 3.7v 350mAh: Lithium ion polymer (also known as 'lipo' or 'lipoly') batteries are thin, light and powerful. The output ranges from 4.2V when completely charged to 3.7V. This battery has a capacity of 350mAh for a total of about 1.3 Wh. The batteries come pre-attached with a genuine 2-pin JST-PH connector as shown and include the necessary protection circuitry.
