# Fritzing sketch robotling_version1_3 (saved by Fritzing 0.9.3b)
circuit board: 6.62cm x 5.85cm
breadboards: 4

parts:
  Motors = female pin header, 4 pins [form="♀ (female)" part_number="Motor connector"]
  MCP3208 = IC, DIP package, 16 pins [chip_label=MCP3208]
  C1 = Tantalum Capacitor [capacitance=1μF package="100 mil [THT, tantalum]"]
  Analog_In = female pin header, 8 pins [form="♀ (female)"]
  Analog_In_b = female pin header, 8 pins [form="♀ (female)"]
  Analog_In_c = female pin header, 8 pins [form="♀ (female)"]
  R1 = Resistor [tolerance=±5% resistance=8.2k package=THT]
  I2C = female pin header, 6 pins [form="♀ (female)"]
  J2 = male pin header, 2 pins [form="♂ (male)"]
  J2_b = male pin header, 2 pins [form="♂ (male)"]
  SN72AHCT125N = IC, DIP package, 14 pins [chip_label=SN72AHCT]
  C2 = Tantalum Capacitor [capacitance=1μF package="100 mil [THT, tantalum]"]
  DIO = female pin header, 4 pins [form="♀ (female)"]
  DIO_c = female pin header, 4 pins [form="♀ (female)"]
  DIO_b = female pin header, 4 pins [form="♀ (female)"]
  R2 = Resistor [tolerance=±5% resistance=8.2k package=THT]
  LiPo_Battery_1100_mAh = Lithium Ion Polymer Battery 3.7v 350mAh [part_number=2750]
  S1 = SPST Switch [package=switch-spdt]
  NP = female pin header, 3 pins [form="♀ (female)"]
  R3 = Resistor [tolerance=±5% resistance=680 package=THT]
  J3 = rounded female pin header, 4 pins [form="♀ (female rounded)"]
  J4 = female pin header, 2 pins [form="♀ (female)"]
  R4 = Resistor [tolerance=±5% resistance=680 package=THT]
  LED1 = LED - 3mm [color="Green (565nm)" package="3 mm [THT]"]
  R5 = Resistor [tolerance=±5% resistance=1k package=THT]
  R6 = Resistor [tolerance=±5% resistance=0 package=THT]
  R8 = Resistor [tolerance=±5% resistance=0 package=THT]
  R9 = Resistor [tolerance=±5% resistance=12k package=THT]
  R10 = Resistor [tolerance=±5% resistance=12k package=THT]
  C3 = Tantalum Capacitor [capacitance=4.7µF voltage=16V package="100 mil [THT, tantalum]"]
  DRV8835 = DRV8835 [package="DIP (Dual Inline) [THT]"]
  J6 = female pin header, 1 pin [form="♀ (female)"]
  J5 = female pin header, 1 pin [form="♀ (female)"]
  C4 = Tantalum Capacitor [capacitance=4.7µF voltage=16V package="100 mil [THT, tantalum]"]
  LSM303 = Flora LSM303 Compass+Accel
  J7 = female pin header, 6 pins [form="♀ (female)"]
  Feather = Adafruit HUZZAH32 ESP32 Feather [part_number="Adafruit #3405"]
  4377 = MAX4377T [package=so08]
  J8 = female pin header, 2 pins [form="♀ (female)"]
  J9 = female pin header, 2 pins [form="♀ (female)"]

nets:
  N1: Motors.pin1, R6.Pin_1, 4377.RS1-
  N2: Motors.pin2, DRV8835.BOUT1
  N3: Motors.pin3, R8.Pin_1, 4377.RS2-
  N4: Motors.pin4, DRV8835.AOUT1
  N5: MCP3208.pin1, Analog_In.pin1
  N6: MCP3208.pin2, Analog_In.pin2
  N7: MCP3208.pin3, Analog_In.pin3
  N8: MCP3208.pin4, Analog_In.pin4
  N9: MCP3208.pin5, Analog_In.pin5
  N10: MCP3208.pin6, Analog_In.pin6
  N11: MCP3208.pin7, Analog_In.pin7
  N12: MCP3208.pin8, Analog_In.pin8
  GND: MCP3208.pin9, MCP3208.pin14, C1.-, Analog_In_b.pin1, Analog_In_b.pin2, Analog_In_b.pin3, Analog_In_b.pin4, Analog_In_b.pin5, Analog_In_b.pin6, Analog_In_b.pin7, Analog_In_b.pin8, I2C.pin6, SN72AHCT125N.pin1, SN72AHCT125N.pin4, SN72AHCT125N.pin7, SN72AHCT125N.pin10, SN72AHCT125N.pin13, C2.-, DIO_c.pin1, DIO_c.pin2, DIO_c.pin3, DIO_c.pin4, LiPo_Battery_1100_mAh.negative, NP.pin1, J3.pin2, LED1.cathode, R5.Pin_0, C3.-, DRV8835.GNDd, DRV8835.GNDm, C4.-, LSM303.GND, J7.pin1, Feather.GND, 4377.GND
  N13: MCP3208.pin10, Feather.A5_IO4
  N14: MCP3208.pin11, Feather.MOSI
  N15: MCP3208.pin12, Feather.MISO
  N16: MCP3208.pin13, Feather.SCK
  N17: MCP3208.pin15, MCP3208.pin16, C1.+, Analog_In_c.pin1, Analog_In_c.pin2, Analog_In_c.pin3, Analog_In_c.pin4, Analog_In_c.pin5, Analog_In_c.pin6, Analog_In_c.pin7, Analog_In_c.pin8, SN72AHCT125N.pin14, C2.+, DIO_b.pin1, DIO_b.pin2, DIO_b.pin3, DIO_b.pin4, NP.pin2, R4.Pin_0, DRV8835.VMM, 4377.VCC
  3.3V: R1.Pin_0, I2C.pin5, R2.Pin_0, DRV8835.VCC, DRV8835.MODE, LSM303.3.3V, J7.pin3, J7.pin6, Feather.3.3V
  N18: R1.Pin_1, I2C.pin4, LSM303.SCL, J7.pin4, Feather.SCL
  N19: I2C.pin1, J3.pin1, DRV8835.VIN
  N20: I2C.pin2, J2_b.pin1
  N21: I2C.pin3, R2.Pin_1, LSM303.SDA, J7.pin5, Feather.SDA
  N22: J2.pin1, J2.pin2, Feather.IO32_A7
  N23: J2_b.pin2, SN72AHCT125N.pin2
  N24: SN72AHCT125N.pin3, DIO.pin1
  N25: SN72AHCT125N.pin5, Feather.IO33_A9
  N26: SN72AHCT125N.pin6, DIO.pin2
  N27: SN72AHCT125N.pin8, DIO.pin4
  N28: SN72AHCT125N.pin9, Feather.IO27_A10
  N29: SN72AHCT125N.pin11, DIO.pin3
  N30: SN72AHCT125N.pin12, Feather.IO13_A12
  N31: LiPo_Battery_1100_mAh.positive, S1.S
  N32: S1.P, J3.pin3, Feather.VBAT
  N33: NP.pin3, R3.Pin_0
  N34: R3.Pin_1, Feather.IO15_A8
  N35: J3.pin4, J4.pin1
  N36: J4.pin2, R5.Pin_1, Feather.IO16
  N37: R4.Pin_1, LED1.anode
  N38: R6.Pin_0, DRV8835.BOUT2, 4377.RS1+
  N39: R8.Pin_0, DRV8835.AOUT2, 4377.RS2+
  N40: R9.Pin_0, 4377.OUT1
  N41: R9.Pin_1, C3.+, J5.pin1
  N42: R10.Pin_0, 4377.OUT2
  N43: R10.Pin_1, J6.pin1, C4.+
  N44: DRV8835.B/EN/IN2, Feather.IO21
  N45: DRV8835.B/PH/IN1, Feather.A1_DAC1
  N46: DRV8835.A/EN/IN2, J8.pin2, J9.pin2
  N47: DRV8835.A/PH/IN1, Feather.IO14_A6
  N48: Feather.A3_I39, J9.pin1
  N49: Feather.A0_DAC2, J8.pin1

notes:
  -MA-
  -MB-
  Vo
  Vi
  g
  7
  Ai G 5V
  gd
  3V
  sd
  sc
  5V
  g 5V d
  3
  0
  D
  >I2C
  >DIO
  (+)
  OFF
  Robotling
  shd
  v1.3
  -A0--A3-

custom parts:
  Lithium Ion Polymer Battery 3.7v 350mAh: Lithium ion polymer (also known as 'lipo' or 'lipoly') batteries are thin, light and powerful. The output ranges from 4.2V when completely charged to 3.7V. This battery has a capacity of 350mAh for a total of about 1.3 Wh. The batteries come pre-attached with a genuine 2-pin JST-PH connector as shown and include the necessary protection circuitry.
  DRV8835: Motor driver by Pololu
  Flora LSM303 Compass+Accel: Add motion and direction sensing to your wearable FLORA project with this high precision 3-axis Accelerometer+Compass sensor. Inside are two sensors, one is a classic 3-axis accelerometer, which can tell you which direction is down towards the Earth (by measuring gravity) or how fast the board is accelerating in 3D space. The other is a magnetometer that can sense where the strongest magnetic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
